// Logisim project ejemploPracticaFinal3.circ as structural Verilog: 15 circuits, main circuit main
module main (
  input  [1:0] in_1,
  input  E1,
  input  E2,
  input  E3,
  input  E4,
  input  [1:0] in_6,
  input  [3:0] A,
  input  [3:0] B,
  input  in_9,
  output out_10,
  output [3:0] out_11,
  output out_12
);

  // decode3 decode3_1: pin names not known; wires that end beside it: E1, E2, E3, E4, in_1, out_10
  // Alu8 alu8_1: pin names not known; wires that end beside it: A, B, in_9, in_6, out_11, out_12
endmodule

module fullAdder (
  input  A,
  input  B,
  input  Cin,
  output A_B,
  output Cout
);

  wire and_1_out_3, and_2_out_3, xor_1_out_3;

  XOR xor_1 (.in_1(A), .in_2(B), .out_3(xor_1_out_3));
  XOR xor_2 (.in_1(xor_1_out_3), .in_2(Cin), .out_3(A_B));
  \and  and_1 (.X(A), .Y(B), .out_3(and_1_out_3));
  \or  or_1 (.X(and_1_out_3), .Y(and_2_out_3), .out_3(Cout));
  \and  and_2 (.X(xor_1_out_3), .Y(Cin), .out_3(and_2_out_3));
endmodule

module decode2 (
  input  [1:0] code,
  output s0,
  output s1,
  output s2,
  output s3
);

  wire not_1_out_2, not_2_out_2;

  Not not_1 (.X(code[0]), .out_2(not_1_out_2));
  Not not_2 (.X(code[1]), .out_2(not_2_out_2));
  \and  and_1 (.X(not_2_out_2), .Y(code[0]), .out_3(s1));
  \and  and_2 (.X(code[1]), .Y(not_1_out_2), .out_3(s2));
  \and  and_3 (.X(not_2_out_2), .Y(not_1_out_2), .out_3(s0));
  \and  and_4 (.X(code[1]), .Y(code[0]), .out_3(s3));
endmodule

// mux
module decode3 (
  input  [1:0] code,
  output s0,
  output s1,
  output s2,
  output s3
);

  wire not_1_out_2, not_2_out_2;

  Not not_1 (.X(code[0]), .out_2(not_1_out_2));
  Not not_2 (.X(code[1]), .out_2(not_2_out_2));
  \and  and_1 (.X(not_2_out_2), .Y(code[0]), .out_3(s1));
  \and  and_2 (.X(not_2_out_2), .Y(not_1_out_2), .out_3(s0));
  \and  and_3 (.X(code[1]), .Y(not_1_out_2), .out_3(s2));
  \and  and_4 (.X(code[1]), .Y(code[0]), .out_3(s3));
endmodule

module mux2 (
  input  [1:0] code,
  input  E0,
  input  E1,
  output Out
);

  wire and_1_out_4, and_2_out_3, and_3_out_3, and_4_out_3, and_5_out_3, and_6_out_3, and_7_out_3,
       decode2_1_s0, decode2_1_s1, decode2_1_s2, decode2_1_s3, or_1_out_3, or_2_out_3, xor_1_out_3,
       xor_2_out_3;

  decode2 decode2_1 (.code(code), .s0(decode2_1_s0), .s1(decode2_1_s1), .s2(decode2_1_s2), .s3(decode2_1_s3));
  AND and_1 (.X(E1), .Y(E0), .X_prime(decode2_1_s0), .out_4(and_1_out_4));
  \and  and_2 (.X(decode2_1_s1), .Y(E0), .out_3(and_2_out_3));
  \and  and_3 (.X(decode2_1_s1), .Y(E1), .out_3(and_3_out_3));
  \and  and_4 (.X(E0), .Y(decode2_1_s2), .out_3(and_4_out_3));
  \or  or_1 (.X(and_3_out_3), .Y(and_2_out_3), .out_3(or_1_out_3));
  XOR xor_1 (.in_1(and_6_out_3), .in_2(and_4_out_3), .out_3(xor_1_out_3));
  \and  and_5 (.X(E1), .Y(decode2_1_s3), .out_3(and_5_out_3));
  \and  and_6 (.X(E1), .Y(decode2_1_s2), .out_3(and_6_out_3));
  \and  and_7 (.X(E0), .Y(decode2_1_s3), .out_3(and_7_out_3));
  \or  or_2 (.X(and_5_out_3), .Y(and_7_out_3), .out_3(or_2_out_3));
  XOR xor_2 (.in_1(decode2_1_s3), .in_2(or_2_out_3), .out_3(xor_2_out_3));
  OR or_3 (.X(and_1_out_4), .Y(or_1_out_3), .X_prime(xor_1_out_3), .Y_prime(xor_2_out_3), .out_5(Out));
endmodule

module mux2_6 (
  input  [1:0] in_1,
  input  E0,
  input  E1,
  input  E2,
  input  E3,
  output out_6
);

  wire decode2_1_s0, decode2_1_s1, decode2_1_s2, decode2_1_s3;

  decode2 decode2_1 (.code(in_1), .s0(decode2_1_s0), .s1(decode2_1_s1), .s2(decode2_1_s2), .s3(decode2_1_s3));
  // mux2 mux2_1: pin names not known; wires that end beside it: decode2_1_s0, decode2_1_s1, decode2_1_s2, decode2_1_s3, E0, E1, E2, E3, out_6
endmodule

module Alu1 (
  input  Cin,
  input  [1:0] in_2,
  input  A,
  input  B,
  output out,
  output Cout
);

  wire and_1_out_3, or_1_out_3;

  \or  or_1 (.X(B), .Y(A), .out_3(or_1_out_3));
  \and  and_1 (.X(B), .Y(A), .out_3(and_1_out_3));
  fullAdder fulladder_1 (.A(A), .B(B), .Cin(Cin), .Cout(Cout));  // open: A_B
  // decode3 decode3_1: pin names not known; wires that end beside it: and_1_out_3, or_1_out_3, in_2, out
endmodule

module Alu8 (
  input  Cinit,
  input  [3:0] A,
  input  [1:0] in_3,
  input  [3:0] B,
  output [3:0] out,
  output overflow
);

  wire alu1_1_cout, alu1_2_cout, alu1_4_cout;

  Alu1 alu1_1 (.A(A[0]), .B(B[0]), .Cin(Cinit), .Cout(alu1_1_cout), .out(out[0]));  // open: in_2
  Alu1 alu1_2 (.A(A[1]), .B(B[1]), .Cin(alu1_1_cout), .Cout(alu1_2_cout), .out(out[1]));  // open: in_2
  Alu1 alu1_3 (.A(A[3]), .B(B[3]), .Cin(alu1_4_cout), .Cout(overflow), .out(out[3]));  // open: in_2
  Alu1 alu1_4 (.A(A[2]), .B(B[2]), .Cin(alu1_2_cout), .Cout(alu1_4_cout), .out(out[2]));  // open: in_2
endmodule

module malSub (
  input  [3:0] A,
  input  [3:0] B,
  output [3:0] out_3
);

  wire [3:0] adder_1_out, not_1_out;

  assign not_1_out = ~B;  // NOT_Gate not_1, 4 bits wide
  Adder #(.width(4)) adder_1 (.a(not_1_out), .b(4'b0001), .out(adder_1_out));  // open: cin, cout
  Adder #(.width(4)) adder_2 (.a(A), .b(adder_1_out), .out(out_3));  // open: cin, cout
endmodule

module \and  (
  input  X,
  input  Y,
  output out_3
);

  wire transistor_1_out;

  Transistor #(.\type ("n")) transistor_1 (.in(1'b1), .out(transistor_1_out), .gate(X));
  Transistor #(.\type ("n")) transistor_2 (.in(transistor_1_out), .out(out_3), .gate(Y));
  Transistor transistor_3 (.in(1'b0), .out(out_3), .gate(Y));
  Transistor transistor_4 (.in(1'b0), .out(out_3), .gate(X));
endmodule

module AND (
  input  X,
  input  Y,
  input  X_prime,
  output out_4
);

  wire transistor_1_out, transistor_2_out;

  Transistor #(.\type ("n")) transistor_1 (.in(1'b1), .out(transistor_1_out), .gate(X));
  Transistor #(.\type ("n")) transistor_2 (.in(transistor_1_out), .out(transistor_2_out), .gate(Y));
  Transistor #(.\type ("n")) transistor_3 (.in(transistor_2_out), .out(out_4), .gate(X_prime));
  Transistor transistor_4 (.in(1'b0), .out(out_4), .gate(Y));
  Transistor transistor_5 (.in(1'b0), .out(out_4), .gate(X_prime));
  Transistor transistor_6 (.in(1'b0), .out(out_4), .gate(X));
endmodule

// OR
module \or  (
  input  X,
  input  Y,
  output out_3
);

  wire transistor_3_out;

  Transistor #(.\type ("n")) transistor_1 (.in(1'b1), .out(out_3), .gate(X));
  Transistor transistor_2 (.in(transistor_3_out), .out(out_3), .gate(X));
  Transistor transistor_3 (.in(1'b0), .out(transistor_3_out), .gate(Y));
  Transistor #(.\type ("n")) transistor_4 (.in(1'b1), .out(out_3), .gate(Y));
endmodule

module OR (
  input  X,
  input  Y,
  input  X_prime,
  input  Y_prime,
  output out_5
);

  wire transistor_3_out, transistor_4_out, transistor_5_out;

  Transistor #(.\type ("n")) transistor_1 (.in(1'b1), .out(out_5), .gate(X));
  Transistor transistor_2 (.in(transistor_3_out), .out(out_5), .gate(X));
  Transistor transistor_3 (.in(transistor_4_out), .out(transistor_3_out), .gate(Y));
  Transistor transistor_4 (.in(transistor_5_out), .out(transistor_4_out), .gate(X_prime));
  Transistor transistor_5 (.in(1'b0), .out(transistor_5_out), .gate(Y_prime));
  Transistor #(.\type ("n")) transistor_6 (.in(1'b1), .out(out_5), .gate(Y));
  Transistor #(.\type ("n")) transistor_7 (.in(1'b1), .out(out_5), .gate(X_prime));
  Transistor #(.\type ("n")) transistor_8 (.in(1'b1), .out(out_5), .gate(Y_prime));
endmodule

module XOR (
  input  in_1,
  input  in_2,
  output out_3
);

  wire transistor_1_out;

  Transistor transistor_1 (.in(1'b1), .out(transistor_1_out), .gate(in_2));
  Transistor #(.\type ("n")) transistor_2 (.in(transistor_1_out), .out(out_3), .gate(in_1));
  Transistor transistor_3 (.in(in_2), .out(out_3), .gate(in_1));
  Transistor #(.\type ("n")) transistor_4 (.in(1'b0), .out(transistor_1_out), .gate(in_2));
endmodule

module Not (
  input  X,
  output out_2
);

  Transistor transistor_1 (.in(1'b1), .out(out_2), .gate(X));
  Transistor #(.\type ("n")) transistor_2 (.in(1'b0), .out(out_2), .gate(X));
endmodule
