// Logisim project main.circ as structural Verilog
module main (
  input  in_1,
  output out_2
);

  Not not_1 (.X(in_1), .out_2(out_2));
endmodule

module \and  (
  input  X,
  input  Y,
  output out_3
);

  wire transistor_1_out;

  Transistor #(.\type ("n")) transistor_1 (.in(1'b1), .out(transistor_1_out), .gate(X));
  Transistor #(.\type ("n")) transistor_2 (.in(transistor_1_out), .out(out_3), .gate(Y));
  Transistor transistor_3 (.in(1'b0), .out(out_3), .gate(Y));
  Transistor transistor_4 (.in(1'b0), .out(out_3), .gate(X));
endmodule

module \or  (
  input  X,
  input  Y,
  output out_3
);

  wire transistor_3_out;

  Transistor #(.\type ("n")) transistor_1 (.in(1'b1), .out(out_3), .gate(X));
  Transistor transistor_2 (.in(transistor_3_out), .out(out_3), .gate(X));
  Transistor transistor_3 (.in(1'b0), .out(transistor_3_out), .gate(Y));
  Transistor #(.\type ("n")) transistor_4 (.in(1'b1), .out(out_3), .gate(Y));
endmodule

module Nand (
  input  X,
  input  Y,
  output out_3
);

  wire transistor_3_out;

  Transistor transistor_1 (.in(1'b1), .out(out_3), .gate(X));
  Transistor #(.\type ("n")) transistor_2 (.in(transistor_3_out), .out(out_3), .gate(X));
  Transistor #(.\type ("n")) transistor_3 (.in(1'b0), .out(transistor_3_out), .gate(Y));
  Transistor transistor_4 (.in(1'b1), .out(out_3), .gate(Y));
endmodule

module Nor (
  input  X,
  input  Y,
  output out_3
);

  wire transistor_1_out;

  Transistor transistor_1 (.in(1'b1), .out(transistor_1_out), .gate(X));
  Transistor transistor_2 (.in(transistor_1_out), .out(out_3), .gate(Y));
  Transistor #(.\type ("n")) transistor_3 (.in(1'b0), .out(out_3), .gate(Y));
  Transistor #(.\type ("n")) transistor_4 (.in(1'b0), .out(out_3), .gate(X));
endmodule

module Not (
  input  X,
  output out_2
);

  Transistor transistor_1 (.in(1'b1), .out(out_2), .gate(X));
  Transistor #(.\type ("n")) transistor_2 (.in(1'b0), .out(out_2), .gate(X));
endmodule

module A_Y___NO_B_____O_____NO_A___Y_B (
  input  A,
  input  B,
  output out_3
);

  wire and_1_out_3, and_2_out_3, not_1_out_2, not_2_out_2;

  Not not_1 (.X(A), .out_2(not_1_out_2));
  Not not_2 (.X(B), .out_2(not_2_out_2));
  \and  and_1 (.X(not_2_out_2), .Y(A), .out_3(and_1_out_3));
  \and  and_2 (.X(B), .Y(not_1_out_2), .out_3(and_2_out_3));
  \or  or_1 (.X(and_2_out_3), .Y(and_1_out_3), .out_3(out_3));
endmodule

module PRIMOS (
  input  E4,
  input  E3,
  input  E1,
  input  E0,
  output out_5
);

  wire and_1_out_5, and_2_out_5, and_3_out_5, and_4_out_5, and_5_out_5, and_6_out_5, not_1_out_2,
       not_2_out_2, not_3_out_2, not_4_out_2;

  Not not_1 (.X(E4), .out_2(not_1_out_2));
  Not not_2 (.X(E3), .out_2(not_2_out_2));
  Not not_3 (.X(E1), .out_2(not_3_out_2));
  Not not_4 (.X(E0), .out_2(not_4_out_2));
  AND and_1 (.X(not_4_out_2), .Y(E1), .X_prime(not_2_out_2), .Y_prime(not_1_out_2), .out_5(and_1_out_5));
  AND and_2 (.X(E0), .Y(E1), .X_prime(not_2_out_2), .Y_prime(not_1_out_2), .out_5(and_2_out_5));
  AND and_3 (.X(E0), .Y(not_3_out_2), .X_prime(E3), .Y_prime(not_1_out_2), .out_5(and_3_out_5));
  OR6 or6_1 (
    .X(and_5_out_5), .Y(and_6_out_5), .Z(and_4_out_5), .X_prime(and_3_out_5), .Y_prime(and_2_out_5),
    .Z_prime_prime(and_1_out_5), .out_7(out_5));
  AND and_4 (.X(E0), .Y(E1), .X_prime(E3), .Y_prime(not_1_out_2), .out_5(and_4_out_5));
  AND and_5 (.X(E0), .Y(not_3_out_2), .X_prime(E3), .Y_prime(E4), .out_5(and_5_out_5));
  AND and_6 (.X(E0), .Y(E1), .X_prime(not_2_out_2), .Y_prime(E4), .out_5(and_6_out_5));
endmodule

module OR (
  input  X,
  input  Y,
  input  X_prime,
  input  Y_prime,
  output out_5
);

  wire transistor_5_out, transistor_6_out, transistor_7_out;

  Transistor #(.\type ("n")) transistor_1 (.in(1'b1), .out(out_5), .gate(X));
  Transistor #(.\type ("n")) transistor_2 (.in(1'b1), .out(out_5), .gate(Y));
  Transistor #(.\type ("n")) transistor_3 (.in(1'b1), .out(out_5), .gate(X_prime));
  Transistor transistor_4 (.in(transistor_5_out), .out(out_5), .gate(X));
  Transistor transistor_5 (.in(transistor_6_out), .out(transistor_5_out), .gate(Y));
  Transistor transistor_6 (.in(transistor_7_out), .out(transistor_6_out), .gate(X_prime));
  Transistor transistor_7 (.in(1'b0), .out(transistor_7_out), .gate(Y_prime));
  Transistor #(.\type ("n")) transistor_8 (.in(1'b1), .out(out_5), .gate(Y_prime));
endmodule

module AND (
  input  X,
  input  Y,
  input  X_prime,
  input  Y_prime,
  output out_5
);

  wire transistor_1_out, transistor_2_out, transistor_3_out;

  Transistor #(.\type ("n")) transistor_1 (.in(1'b1), .out(transistor_1_out), .gate(X));
  Transistor #(.\type ("n")) transistor_2 (.in(transistor_1_out), .out(transistor_2_out), .gate(Y));
  Transistor #(.\type ("n")) transistor_3 (.in(transistor_2_out), .out(transistor_3_out), .gate(X_prime));
  Transistor #(.\type ("n")) transistor_4 (.in(transistor_3_out), .out(out_5), .gate(Y_prime));
  Transistor transistor_5 (.in(1'b0), .out(out_5), .gate(Y));
  Transistor transistor_6 (.in(1'b0), .out(out_5), .gate(X_prime));
  Transistor transistor_7 (.in(1'b0), .out(out_5), .gate(Y_prime));
  Transistor transistor_8 (.in(1'b0), .out(out_5), .gate(X));
endmodule

module OR6 (
  input  X,
  input  Y,
  input  Z,
  input  X_prime,
  input  Y_prime,
  input  Z_prime_prime,
  output out_7
);

  wire transistor_3_out, transistor_4_out, transistor_5_out, transistor_6_out, transistor_7_out;

  Transistor #(.\type ("n")) transistor_1 (.in(1'b1), .out(out_7), .gate(X));
  Transistor transistor_2 (.in(transistor_3_out), .out(out_7), .gate(X));
  Transistor transistor_3 (.in(transistor_4_out), .out(transistor_3_out), .gate(Y));
  Transistor transistor_4 (.in(transistor_5_out), .out(transistor_4_out), .gate(Z));
  Transistor transistor_5 (.in(transistor_6_out), .out(transistor_5_out), .gate(X_prime));
  Transistor transistor_6 (.in(transistor_7_out), .out(transistor_6_out), .gate(Y_prime));
  Transistor transistor_7 (.in(1'b0), .out(transistor_7_out), .gate(Z_prime_prime));
  Transistor #(.\type ("n")) transistor_8 (.in(1'b1), .out(out_7), .gate(Y));
  Transistor #(.\type ("n")) transistor_9 (.in(1'b1), .out(out_7), .gate(Z));
  Transistor #(.\type ("n")) transistor_10 (.in(1'b1), .out(out_7), .gate(X_prime));
  Transistor #(.\type ("n")) transistor_11 (.in(1'b1), .out(out_7), .gate(Y_prime));
  Transistor #(.\type ("n")) transistor_12 (.in(1'b1), .out(out_7), .gate(Z_prime_prime));
endmodule

module COMPLEMENTO_A_2 (
  input  E2,
  input  E1,
  input  E0,
  output S2,
  output S1,
  output S0
);

  wire nor_1_out_3, not_1_out_2, not_2_out_2, not_3_out_2, not_4_out_2;

  Not not_1 (.X(E2), .out_2(not_1_out_2));
  Not not_2 (.X(E1), .out_2(not_2_out_2));
  Not not_3 (.X(E0), .out_2(not_3_out_2));
  Nor nor_1 (.X(S1), .Y(S0), .out_3(nor_1_out_3));
  Xor xor_1 (.X(nor_1_out_3), .Y(not_1_out_2), .out_3(S2));
  Not not_4 (.X(S0), .out_2(not_4_out_2));
  Xor xor_2 (.X(not_4_out_2), .Y(not_2_out_2), .out_3(S1));
  Xor xor_3 (.X(1'b1), .Y(not_3_out_2), .out_3(S0));
endmodule

module Pruebas (
  input  in_1,
  input  in_2,
  output out_3
);

  wire transistor_1_out;

  Transistor transistor_1 (.in(1'b1), .out(transistor_1_out), .gate(in_2));
  Transistor #(.\type ("n")) transistor_2 (.in(transistor_1_out), .out(out_3), .gate(in_1));
  Transistor transistor_3 (.in(in_2), .out(out_3), .gate(in_1));
  Transistor #(.\type ("n")) transistor_4 (.in(1'b0), .out(transistor_1_out), .gate(in_2));
endmodule

module PLANTA_DE_SEGURIDAD (
  input  Filtro_1,
  input  Filtro_2,
  input  Filtro_3,
  output out_4,
  output out_5
);

  wire and_1_out_3, and_2_out_3, and_3_out_3, xor_1_out_3;

  Xor xor_1 (.X(Filtro_2), .Y(Filtro_3), .out_3(xor_1_out_3));
  \and  and_1 (.X(Filtro_2), .Y(Filtro_3), .out_3(and_1_out_3));
  Xor xor_2 (.X(Filtro_1), .Y(xor_1_out_3), .out_3(out_5));
  \and  and_2 (.X(Filtro_1), .Y(Filtro_2), .out_3(and_2_out_3));
  \and  and_3 (.X(Filtro_1), .Y(Filtro_3), .out_3(and_3_out_3));
  OR or_1 (.X(and_2_out_3), .Y(and_3_out_3), .X_prime(and_1_out_3), .Y_prime(and_1_out_3), .out_5(out_4));
endmodule

// Xor
module Xor (
  input  X,
  input  Y,
  output out_3
);

  wire transistor_1_out, transistor_4_out, transistor_5_out, transistor_8_out;

  Transistor transistor_1 (.in(1'b1), .out(transistor_1_out), .gate(Y));
  Transistor #(.\type ("n")) transistor_2 (.in(transistor_1_out), .out(out_3), .gate(X));
  Transistor #(.\type ("n")) transistor_3 (.in(transistor_4_out), .out(out_3), .gate(Y));
  Transistor #(.\type ("n")) transistor_4 (.in(1'b0), .out(transistor_4_out), .gate(X));
  Transistor transistor_5 (.in(1'b1), .out(transistor_5_out), .gate(X));
  Transistor #(.\type ("n")) transistor_6 (.in(transistor_5_out), .out(out_3), .gate(Y));
  Transistor transistor_7 (.in(transistor_8_out), .out(out_3), .gate(X));
  Transistor transistor_8 (.in(1'b0), .out(transistor_8_out), .gate(Y));
endmodule

module P____Q (
  input  P,
  input  Q,
  output out_3
);

  wire not_1_out_2;

  Not not_1 (.X(P), .out_2(not_1_out_2));
  \or  or_1 (.X(not_1_out_2), .Y(Q), .out_3(out_3));
endmodule

module SEGURIDAD (
  input  Filtro_1,
  input  Filtro_2,
  input  Filtro_3,
  output Notificacion,
  output Retirarse_calmadamente,
  output Evacuar_Inmediatamente
);

  wire and_1_out_3, and_2_out_3, and_3_out_3, and_4_out_3, and_5_out_3, and_6_out_3, and_7_out_3,
       and_8_out_3, or_1_out_3, or_2_out_3, or_3_out_3, xor_1_out_3, xor_2_out_3, xor_3_out_3, xor_4_out_3;

  \and  and_1 (.X(Filtro_1), .Y(Filtro_2), .out_3(and_1_out_3));
  \and  and_2 (.X(and_1_out_3), .Y(and_3_out_3), .out_3(and_2_out_3));
  \and  and_3 (.X(Filtro_1), .Y(Filtro_3), .out_3(and_3_out_3));
  \and  and_4 (.X(and_3_out_3), .Y(and_5_out_3), .out_3(and_4_out_3));
  \and  and_5 (.X(Filtro_2), .Y(Filtro_3), .out_3(and_5_out_3));
  \and  and_6 (.X(Filtro_1), .Y(Filtro_2), .out_3(and_6_out_3));
  Xor xor_1 (.X(and_6_out_3), .Y(and_7_out_3), .out_3(xor_1_out_3));
  \and  and_7 (.X(Filtro_1), .Y(Filtro_3), .out_3(and_7_out_3));
  Xor xor_2 (.X(and_7_out_3), .Y(and_8_out_3), .out_3(xor_2_out_3));
  \and  and_8 (.X(Filtro_2), .Y(Filtro_3), .out_3(and_8_out_3));
  \and  and_9 (.X(and_2_out_3), .Y(and_4_out_3), .out_3(Evacuar_Inmediatamente));
  \or  or_1 (.X(Filtro_1), .Y(Filtro_2), .out_3(or_1_out_3));
  Xor xor_3 (.X(or_1_out_3), .Y(or_2_out_3), .out_3(xor_3_out_3));
  \or  or_2 (.X(Filtro_1), .Y(Filtro_3), .out_3(or_2_out_3));
  Xor xor_4 (.X(or_2_out_3), .Y(or_3_out_3), .out_3(xor_4_out_3));
  \or  or_3 (.X(Filtro_2), .Y(Filtro_3), .out_3(or_3_out_3));
  \or  or_4 (.X(xor_1_out_3), .Y(xor_2_out_3), .out_3(Retirarse_calmadamente));
  \or  or_5 (.X(xor_3_out_3), .Y(xor_4_out_3), .out_3(Notificacion));
endmodule

module Xor_2 (
  input  X,
  input  Y,
  output out_3
);

  wire transistor_1_out, transistor_4_out, transistor_5_out, transistor_8_out;

  Transistor transistor_1 (.in(1'b1), .out(transistor_1_out), .gate(Y));
  Transistor #(.\type ("n")) transistor_2 (.in(transistor_1_out), .out(out_3), .gate(X));
  Transistor #(.\type ("n")) transistor_3 (.in(transistor_4_out), .out(out_3), .gate(Y));
  Transistor #(.\type ("n")) transistor_4 (.in(1'b0), .out(transistor_4_out), .gate(X));
  Transistor transistor_5 (.in(1'b1), .out(transistor_5_out), .gate(X));
  Transistor #(.\type ("n")) transistor_6 (.in(transistor_5_out), .out(out_3), .gate(Y));
  Transistor transistor_7 (.in(transistor_8_out), .out(out_3), .gate(X));
  Transistor transistor_8 (.in(1'b0), .out(transistor_8_out), .gate(Y));
endmodule

module XOR (
  input  in_1,
  input  in_2,
  output out_3
);

  wire transistor_1_out;

  Transistor transistor_1 (.in(1'b1), .out(transistor_1_out), .gate(in_2));
  Transistor #(.\type ("n")) transistor_2 (.in(transistor_1_out), .out(out_3), .gate(in_1));
  Transistor transistor_3 (.in(in_2), .out(out_3), .gate(in_1));
  Transistor #(.\type ("n")) transistor_4 (.in(1'b0), .out(transistor_1_out), .gate(in_2));
endmodule

module NXOR (
  input  in_1,
  input  in_2,
  output out_3
);

  wire transistor_1_out;

  Transistor transistor_1 (.in(1'b1), .out(transistor_1_out), .gate(in_2));
  Transistor transistor_2 (.in(transistor_1_out), .out(out_3), .gate(in_1));
  Transistor #(.\type ("n")) transistor_3 (.in(in_2), .out(out_3), .gate(in_1));
  Transistor #(.\type ("n")) transistor_4 (.in(1'b0), .out(transistor_1_out), .gate(in_2));
endmodule

module OR3 (
  input  X,
  input  Y,
  input  Z,
  output out_4
);

  wire transistor_3_out, transistor_4_out;

  Transistor #(.\type ("n")) transistor_1 (.in(1'b1), .out(out_4), .gate(X));
  Transistor transistor_2 (.in(transistor_3_out), .out(out_4), .gate(X));
  Transistor transistor_3 (.in(transistor_4_out), .out(transistor_3_out), .gate(Y));
  Transistor transistor_4 (.in(1'b0), .out(transistor_4_out), .gate(Z));
  Transistor #(.\type ("n")) transistor_5 (.in(1'b1), .out(out_4), .gate(Y));
  Transistor #(.\type ("n")) transistor_6 (.in(1'b1), .out(out_4), .gate(Z));
endmodule

module AND3 (
  input  X,
  input  Y,
  input  X_prime,
  output out_4
);

  wire transistor_1_out, transistor_2_out;

  Transistor #(.\type ("n")) transistor_1 (.in(1'b1), .out(transistor_1_out), .gate(X));
  Transistor #(.\type ("n")) transistor_2 (.in(transistor_1_out), .out(transistor_2_out), .gate(Y));
  Transistor #(.\type ("n")) transistor_3 (.in(transistor_2_out), .out(out_4), .gate(X_prime));
  Transistor transistor_4 (.in(1'b0), .out(out_4), .gate(X));
  Transistor transistor_5 (.in(1'b0), .out(out_4), .gate(Y));
  Transistor transistor_6 (.in(1'b0), .out(out_4), .gate(X_prime));
endmodule

module AND6 (
  input  X,
  input  Y,
  input  Z,
  input  X_prime,
  input  Y_prime,
  input  Z_prime,
  output out_7
);

  wire transistor_1_out, transistor_2_out, transistor_3_out, transistor_4_out, transistor_5_out;

  Transistor #(.\type ("n")) transistor_1 (.in(1'b1), .out(transistor_1_out), .gate(X));
  Transistor #(.\type ("n")) transistor_2 (.in(transistor_1_out), .out(transistor_2_out), .gate(Y));
  Transistor #(.\type ("n")) transistor_3 (.in(transistor_2_out), .out(transistor_3_out), .gate(Z));
  Transistor #(.\type ("n")) transistor_4 (.in(transistor_3_out), .out(transistor_4_out), .gate(X_prime));
  Transistor #(.\type ("n")) transistor_5 (.in(transistor_4_out), .out(transistor_5_out), .gate(Y_prime));
  Transistor #(.\type ("n")) transistor_6 (.in(transistor_5_out), .out(out_7), .gate(Z_prime));
  Transistor transistor_7 (.in(1'b0), .out(out_7), .gate(Y_prime));
  Transistor transistor_8 (.in(1'b0), .out(out_7), .gate(Z_prime));
  Transistor transistor_9 (.in(1'b0), .out(out_7), .gate(Y));
  Transistor transistor_10 (.in(1'b0), .out(out_7), .gate(Z));
  Transistor transistor_11 (.in(1'b0), .out(out_7), .gate(X_prime));
  Transistor transistor_12 (.in(1'b0), .out(out_7), .gate(X));
endmodule

module Automatas (
  input  in_1,
  output [1:0] out_2,
  output E1,
  output no_e1,
  output e2,
  output no_2e
);

  wire and_1_out_3, and_2_out_3, and_3_out_3, and_4_out_3, clock_1_out, not_1_out_2, or_1_out_3, or_2_out_3;

  Not not_1 (.X(in_1), .out_2(not_1_out_2));
  \and  and_1 (.X(no_2e), .Y(in_1), .out_3(and_1_out_3));
  \and  and_2 (.X(E1), .Y(in_1), .out_3(and_2_out_3));
  \and  and_3 (.X(e2), .Y(not_1_out_2), .out_3(and_3_out_3));
  Clock clock_1 (.out(clock_1_out));
  \and  and_4 (.X(no_e1), .Y(not_1_out_2), .out_3(and_4_out_3));
  \or  or_1 (.X(and_4_out_3), .Y(and_2_out_3), .out_3(or_1_out_3));
  \or  or_2 (.X(and_3_out_3), .Y(and_1_out_3), .out_3(or_2_out_3));
  D_Flip_Flop d_ff_1 (.clk(clock_1_out), .D(or_1_out_3), .Q(E1), .Qn(no_e1));  // open: preset, en, reset
  D_Flip_Flop d_ff_2 (.clk(clock_1_out), .D(or_2_out_3), .Q(e2), .Qn(no_2e));  // open: preset, en, reset

  assign out_2 = {E1, e2};
endmodule

module Adder2 (
  input  Cin,
  input  A,
  input  B,
  output A_B,
  output Cout
);

  wire and3_1_out_4, and3_2_out_4, and3_3_out_4, and3_4_out_4, and3_5_out_4, and_1_out_3, not_1_out_2,
       not_2_out_2, not_3_out_2;

  Not not_1 (.X(Cin), .out_2(not_1_out_2));
  Not not_2 (.X(A), .out_2(not_2_out_2));
  Not not_3 (.X(B), .out_2(not_3_out_2));
  \and  and_1 (.X(A), .Y(B), .out_3(and_1_out_3));
  AND3 and3_1 (.X(A), .Y(not_3_out_2), .X_prime(Cin), .out_4(and3_1_out_4));
  AND3 and3_2 (.X(not_2_out_2), .Y(B), .X_prime(Cin), .out_4(and3_2_out_4));
  OR3 or3_1 (.X(and3_1_out_4), .Y(and3_2_out_4), .Z(and_1_out_3), .out_4(Cout));
  AND3 and3_3 (.X(not_2_out_2), .Y(B), .X_prime(not_1_out_2), .out_4(and3_3_out_4));
  AND3 and3_4 (.X(not_2_out_2), .Y(not_3_out_2), .X_prime(Cin), .out_4(and3_4_out_4));
  AND3 and3_5 (.X(A), .Y(not_3_out_2), .X_prime(not_1_out_2), .out_4(and3_5_out_4));
  OR3 or3_2 (.X(and3_4_out_4), .Y(and3_3_out_4), .Z(and3_5_out_4), .out_4(A_B));
endmodule

module Suc2 (
  input  Cin,
  input  A,
  input  B,
  output A_B,
  output Cout
);

  wire and3_1_out_4, and3_2_out_4, and3_3_out_4, and3_4_out_4, and_1_out_3, and_2_out_3, not_1_out_2,
       not_2_out_2, not_3_out_2;

  Not not_1 (.X(Cin), .out_2(not_1_out_2));
  Not not_2 (.X(A), .out_2(not_2_out_2));
  Not not_3 (.X(B), .out_2(not_3_out_2));
  \and  and_1 (.X(not_2_out_2), .Y(B), .out_3(and_1_out_3));
  AND3 and3_1 (.X(not_2_out_2), .Y(not_3_out_2), .X_prime(Cin), .out_4(and3_1_out_4));
  AND3 and3_2 (.X(A), .Y(B), .X_prime(Cin), .out_4(and3_2_out_4));
  AND3 and3_3 (.X(A), .Y(not_3_out_2), .X_prime(not_1_out_2), .out_4(and3_3_out_4));
  OR or_1 (.X(and3_3_out_4), .Y(and3_2_out_4), .X_prime(and3_1_out_4), .Y_prime(and_1_out_3), .out_5(A_B));
  \and  and_2 (.X(not_2_out_2), .Y(B), .out_3(and_2_out_3));
  \or  or_2 (.X(and3_4_out_4), .Y(and_2_out_3), .out_3(Cout));
  AND3 and3_4 (.X(not_2_out_2), .Y(not_3_out_2), .X_prime(Cin), .out_4(and3_4_out_4));
endmodule

module decode2 (
  input  [1:0] code,
  output s0,
  output s1,
  output s2,
  output s3
);

  wire not_1_out_2, not_2_out_2;

  Not not_1 (.X(code[0]), .out_2(not_1_out_2));
  Not not_2 (.X(code[1]), .out_2(not_2_out_2));
  \and  and_1 (.X(not_2_out_2), .Y(not_1_out_2), .out_3(s0));
  \and  and_2 (.X(not_2_out_2), .Y(code[0]), .out_3(s1));
  \and  and_3 (.X(code[1]), .Y(not_1_out_2), .out_3(s2));
  \and  and_4 (.X(code[1]), .Y(code[0]), .out_3(s3));
endmodule

module mux2 (
  input  [1:0] code,
  input  C1,
  input  A,
  input  B,
  output Out,
  output Cout
);

  wire adder2_1_a_b, adder2_1_cout, and_1_out_5, and_2_out_3, and_3_out_3, and_4_out_3, and_5_out_3,
       and_6_out_3, and_7_out_3, and_8_out_3, and_9_out_3, decode2_1_s0, decode2_1_s1, decode2_1_s2,
       decode2_1_s3, or_1_out_3, suc2_1_a_b, suc2_1_cout;

  decode2 decode2_1 (.code(code), .s0(decode2_1_s0), .s1(decode2_1_s1), .s2(decode2_1_s2), .s3(decode2_1_s3));
  AND and_1 (.X(A), .Y(B), .X_prime(decode2_1_s0), .Y_prime(decode2_1_s0), .out_5(and_1_out_5));
  \and  and_2 (.X(decode2_1_s1), .Y(A), .out_3(and_2_out_3));
  \and  and_3 (.X(decode2_1_s1), .Y(B), .out_3(and_3_out_3));
  \or  or_1 (.X(and_2_out_3), .Y(and_3_out_3), .out_3(or_1_out_3));
  \and  and_4 (.X(A), .Y(decode2_1_s2), .out_3(and_4_out_3));
  \and  and_5 (.X(B), .Y(decode2_1_s2), .out_3(and_5_out_3));
  Adder2 adder2_1 (.A(and_4_out_3), .B(and_5_out_3), .Cin(and_8_out_3), .A_B(adder2_1_a_b), .Cout(adder2_1_cout));
  \and  and_6 (.X(B), .Y(decode2_1_s3), .out_3(and_6_out_3));
  \and  and_7 (.X(A), .Y(decode2_1_s3), .out_3(and_7_out_3));
  \and  and_8 (.X(C1), .Y(decode2_1_s2), .out_3(and_8_out_3));
  Suc2 suc2_1 (.A(and_7_out_3), .B(and_6_out_3), .Cin(and_9_out_3), .A_B(suc2_1_a_b), .Cout(suc2_1_cout));
  \and  and_9 (.X(C1), .Y(decode2_1_s3), .out_3(and_9_out_3));
  OR or_2 (.X(and_1_out_5), .Y(or_1_out_3), .X_prime(adder2_1_a_b), .Y_prime(suc2_1_a_b), .out_5(Out));
  \or  or_3 (.X(adder2_1_cout), .Y(suc2_1_cout), .out_3(Cout));
endmodule

module Alu1 (
  input  Cin,
  input  [1:0] Operacion,
  input  A,
  input  B,
  output out,
  output Cout
);

  mux2 mux2_1 (.A(A), .B(B), .C1(Cin), .code(Operacion), .Out(out), .Cout(Cout));
endmodule

module Alu8 (
  input  Cinit,
  input  [1:0] Operacion,
  input  [7:0] A,
  input  [7:0] B,
  output [7:0] S,
  output out_6
);

  wire alu1_1_cout, alu1_2_cout, alu1_3_cout, alu1_4_cout, alu1_5_cout, alu1_6_cout, alu1_7_cout;

  Alu1 alu1_1 (.A(A[0]), .B(B[0]), .Cin(Cinit), .Operacion(Operacion), .Cout(alu1_1_cout), .out(S[0]));
  Alu1 alu1_2 (.A(A[1]), .B(B[1]), .Cin(alu1_1_cout), .Operacion(Operacion), .Cout(alu1_2_cout), .out(S[1]));
  Alu1 alu1_3 (.A(A[2]), .B(B[2]), .Cin(alu1_2_cout), .Operacion(Operacion), .Cout(alu1_3_cout), .out(S[2]));
  Alu1 alu1_4 (.A(A[3]), .B(B[3]), .Cin(alu1_3_cout), .Operacion(Operacion), .Cout(alu1_4_cout), .out(S[3]));
  Alu1 alu1_5 (.A(A[4]), .B(B[4]), .Cin(alu1_4_cout), .Operacion(Operacion), .Cout(alu1_5_cout), .out(S[4]));
  Alu1 alu1_6 (.A(A[5]), .B(B[5]), .Cin(alu1_5_cout), .Operacion(Operacion), .Cout(alu1_6_cout), .out(S[5]));
  Alu1 alu1_7 (.A(A[6]), .B(B[6]), .Cin(alu1_6_cout), .Operacion(Operacion), .Cout(alu1_7_cout), .out(S[6]));
  Alu1 alu1_8 (.A(A[7]), .B(B[7]), .Cin(alu1_7_cout), .Operacion(Operacion), .Cout(out_6), .out(S[7]));
endmodule

module Complemento (
  input  E0,
  input  E1,
  output S0,
  output S1
);

  wire not_1_out_2, not_2_out_2, not_3_out_2;

  Not not_1 (.X(E1), .out_2(not_1_out_2));
  Not not_2 (.X(E0), .out_2(not_2_out_2));
  Not not_3 (.X(S0), .out_2(not_3_out_2));
  XOR xor_1 (.in_1(not_3_out_2), .in_2(not_1_out_2), .out_3(S1));
  XOR xor_2 (.in_1(1'b1), .in_2(not_2_out_2), .out_3(S0));
endmodule

module Decode3 (
  input  [2:0] code,
  output s0,
  output s1,
  output s2,
  output s3,
  output s4,
  output s5,
  output s6,
  output s7
);

  wire not_1_out_2, not_2_out_2, not_3_out_2;

  Not not_1 (.X(code[0]), .out_2(not_1_out_2));
  Not not_2 (.X(code[1]), .out_2(not_2_out_2));
  Not not_3 (.X(code[2]), .out_2(not_3_out_2));
  AND3 and3_1 (.X(not_3_out_2), .Y(not_2_out_2), .X_prime(not_1_out_2), .out_4(s0));
  AND3 and3_2 (.X(not_3_out_2), .Y(code[1]), .X_prime(code[0]), .out_4(s3));
  AND3 and3_3 (.X(not_3_out_2), .Y(code[1]), .X_prime(not_1_out_2), .out_4(s2));
  AND3 and3_4 (.X(not_3_out_2), .Y(not_2_out_2), .X_prime(code[0]), .out_4(s1));
  AND3 and3_5 (.X(code[2]), .Y(not_2_out_2), .X_prime(code[0]), .out_4(s5));
  AND3 and3_6 (.X(code[2]), .Y(not_2_out_2), .X_prime(not_1_out_2), .out_4(s4));
  AND3 and3_7 (.X(code[2]), .Y(code[1]), .X_prime(not_1_out_2), .out_4(s6));
  AND3 and3_8 (.X(code[2]), .Y(code[1]), .X_prime(code[0]), .out_4(s7));
endmodule

module Mux3 (
  input  [2:0] code,
  input  C1,
  input  A,
  input  B,
  output Out,
  output Cout
);

  wire adder2_1_a_b, adder2_1_cout, and_1_out_5, and_2_out_3, and_3_out_3, and_4_out_3, and_5_out_3,
       and_6_out_3, and_7_out_3, and_8_out_3, and_9_out_3, decode3_1_p2, decode3_1_p3, decode3_1_p4,
       decode3_1_p5, or_1_out_3, suc2_1_a_b, suc2_1_cout;

  // Decode3 decode3_1: pin names not known; wires that end beside it: code, decode3_1_p2, decode3_1_p3, decode3_1_p4, decode3_1_p5
  AND and_1 (.X(A), .Y(B), .X_prime(decode3_1_p2), .Y_prime(decode3_1_p2), .out_5(and_1_out_5));
  \and  and_2 (.X(decode3_1_p3), .Y(A), .out_3(and_2_out_3));
  \and  and_3 (.X(decode3_1_p3), .Y(B), .out_3(and_3_out_3));
  \and  and_4 (.X(B), .Y(decode3_1_p4), .out_3(and_4_out_3));
  \or  or_1 (.X(and_2_out_3), .Y(and_3_out_3), .out_3(or_1_out_3));
  \and  and_5 (.X(A), .Y(decode3_1_p4), .out_3(and_5_out_3));
  \and  and_6 (.X(C1), .Y(decode3_1_p4), .out_3(and_6_out_3));
  Adder2 adder2_1 (.A(and_5_out_3), .B(and_4_out_3), .Cin(and_6_out_3), .A_B(adder2_1_a_b), .Cout(adder2_1_cout));
  \and  and_7 (.X(C1), .Y(decode3_1_p5), .out_3(and_7_out_3));
  \and  and_8 (.X(B), .Y(decode3_1_p5), .out_3(and_8_out_3));
  \and  and_9 (.X(A), .Y(decode3_1_p5), .out_3(and_9_out_3));
  Suc2 suc2_1 (.A(and_9_out_3), .B(and_8_out_3), .Cin(and_7_out_3), .A_B(suc2_1_a_b), .Cout(suc2_1_cout));
  OR or_2 (.X(and_1_out_5), .Y(or_1_out_3), .X_prime(adder2_1_a_b), .Y_prime(suc2_1_a_b), .out_5(Out));
  \or  or_3 (.X(adder2_1_cout), .Y(suc2_1_cout), .out_3(Cout));
endmodule

module Registro (
  input  in_1,
  input  in_2,
  output out_3,
  output out_4
);

  wire clock_1_out;

  Clock clock_1 (.out(clock_1_out));
  S_R_Flip_Flop s_r_ff_1 (.Q(out_3), .Qn(out_4), .preset(in_1), .reset(in_2), .en(clock_1_out));  // open: S, clk, R
endmodule
