// Logisim project practica3.circ as structural Verilog: 6 circuits, main circuit AND y OR
module AND_y_OR (
  input  A,
  input  B,
  input  Op,
  output S
);

  wire and_1_out, or_1_out;

  and and_1 (and_1_out, A, B);
  or or_1 (or_1_out, A, B);
  Multiplexer #(.enable("false")) multiplexer_1 (.in0(and_1_out), .in1(or_1_out), .out(S), .sel(Op));
endmodule

// full adder
module Sumador_Completo (
  input  Cin,
  input  A,
  input  B,
  output Cout,
  output S
);

  wire and_1_out, and_2_out, and_3_out, and_4_out, and_5_out, and_6_out, and_7_out, not_1_out, not_2_out,
       not_3_out;

  not not_1 (not_1_out, Cin);
  not not_2 (not_2_out, A);
  not not_3 (not_3_out, B);
  and and_1 (and_1_out, Cin, B);
  and and_2 (and_2_out, A, B);
  and and_3 (and_3_out, Cin, A);
  or or_1 (Cout, and_1_out, and_2_out, and_3_out);
  and and_4 (and_4_out, Cin, not_2_out, not_3_out);
  and and_5 (and_5_out, not_1_out, not_2_out, B);
  and and_6 (and_6_out, Cin, A, B);
  and and_7 (and_7_out, not_1_out, A, not_3_out);
  or or_2 (S, and_4_out, and_5_out, and_6_out, and_7_out);
endmodule

module ALU_1_bit (
  input  A,
  input  B,
  input  [1:0] Op,
  input  Cin,
  output S,
  output Cout
);

  wire and_1_out, not_1_out, or_1_out, sumador_completo_1_cout, sumador_completo_1_s;

  Sumador_Completo sumador_completo_1 (
    .Cin(Cin), .A(A), .B(B), .Cout(sumador_completo_1_cout), .S(sumador_completo_1_s));
  and and_1 (and_1_out, A, B);
  or or_1 (or_1_out, A, B);
  Multiplexer #(.select(2), .enable("false")) multiplexer_1 (
    .in0(and_1_out), .in1(or_1_out), .in2(sumador_completo_1_s), .out(S), .sel(Op));  // open: in3
  not not_1 (not_1_out, Op[0]);
  and and_2 (Cout, not_1_out, Op[1], sumador_completo_1_cout);
endmodule

module ALU_8_bits (
  input  [7:0] A,
  input  [1:0] Op,
  input  Cin,
  input  [7:0] B,
  output [7:0] S,
  output out_6
);

  wire alu_1_bit_1_cout, alu_1_bit_2_cout, alu_1_bit_3_cout, alu_1_bit_4_cout, alu_1_bit_5_cout,
       alu_1_bit_6_cout, alu_1_bit_7_cout;

  ALU_1_bit alu_1_bit_1 (.A(A[0]), .B(B[0]), .Cin(Cin), .Op(Op), .S(S[0]), .Cout(alu_1_bit_1_cout));
  ALU_1_bit alu_1_bit_2 (.A(A[1]), .B(B[1]), .Cin(alu_1_bit_1_cout), .Op(Op), .S(S[1]), .Cout(alu_1_bit_2_cout));
  ALU_1_bit alu_1_bit_3 (.A(A[2]), .B(B[2]), .Cin(alu_1_bit_2_cout), .Op(Op), .S(S[2]), .Cout(alu_1_bit_3_cout));
  ALU_1_bit alu_1_bit_4 (.A(A[3]), .B(B[3]), .Cin(alu_1_bit_3_cout), .Op(Op), .S(S[3]), .Cout(alu_1_bit_4_cout));
  ALU_1_bit alu_1_bit_5 (.A(A[4]), .B(B[4]), .Cin(alu_1_bit_4_cout), .Op(Op), .S(S[4]), .Cout(alu_1_bit_5_cout));
  ALU_1_bit alu_1_bit_6 (.A(A[5]), .B(B[5]), .Cin(alu_1_bit_5_cout), .Op(Op), .S(S[5]), .Cout(alu_1_bit_6_cout));
  ALU_1_bit alu_1_bit_7 (.A(A[6]), .B(B[6]), .Cin(alu_1_bit_6_cout), .Op(Op), .S(S[6]), .Cout(alu_1_bit_7_cout));
  ALU_1_bit alu_1_bit_8 (.A(A[7]), .B(B[7]), .Cin(alu_1_bit_7_cout), .Op(Op), .S(S[7]), .Cout(out_6));
endmodule

module \Sustracción  (
  input  A,
  input  B,
  input  [1:0] Op,
  input  Cin,
  output S,
  output Cout
);

  wire and_1_out, multiplexer_1_out, not_1_out, not_2_out, or_1_out, sumador_completo_1_cout,
       sumador_completo_1_s;

  not not_1 (not_1_out, B);
  Sumador_Completo sumador_completo_1 (
    .Cin(Cin), .A(A), .B(multiplexer_1_out), .Cout(sumador_completo_1_cout), .S(sumador_completo_1_s));
  and and_1 (and_1_out, A, B);
  or or_1 (or_1_out, A, B);
  Multiplexer #(.enable("false")) multiplexer_1 (.in0(B), .in1(not_1_out), .out(multiplexer_1_out), .sel(Cin));
  Multiplexer #(.select(2), .enable("false")) multiplexer_2 (
    .in0(and_1_out), .in1(or_1_out), .in2(sumador_completo_1_s), .out(S), .sel(Op));  // open: in3
  not not_2 (not_2_out, Op[0]);
  and and_2 (Cout, not_2_out, Op[1], sumador_completo_1_cout);
endmodule

module ALU_8_bits_Resta (
  input  [7:0] A,
  input  [1:0] Op,
  input  [7:0] B,
  output [7:0] S,
  output out_5
);

  wire and_2_out, not_1_out, \sustracción_1_cout , \sustracción_2_cout , \sustracción_3_cout ,
       \sustracción_4_cout , \sustracción_5_cout , \sustracción_6_cout , \sustracción_7_cout ;
  wire [0:0] and_1_out;

  \Sustracción  \sustracción_1  (
    .A(A[0]), .B(B[0]), .Cin(and_2_out), .Op({Op[1], and_1_out[0]}), .S(S[0]), .Cout(\sustracción_1_cout ));
  \Sustracción  \sustracción_2  (
    .A(A[1]), .B(B[1]), .Cin(\sustracción_1_cout ), .Op({Op[1], and_1_out[0]}), .S(S[1]),
    .Cout(\sustracción_2_cout ));
  \Sustracción  \sustracción_3  (
    .A(A[2]), .B(B[2]), .Cin(\sustracción_2_cout ), .Op({Op[1], and_1_out[0]}), .S(S[2]),
    .Cout(\sustracción_3_cout ));
  \Sustracción  \sustracción_4  (
    .A(A[3]), .B(B[3]), .Cin(\sustracción_3_cout ), .Op({Op[1], and_1_out[0]}), .S(S[3]),
    .Cout(\sustracción_4_cout ));
  \Sustracción  \sustracción_5  (
    .A(A[4]), .B(B[4]), .Cin(\sustracción_4_cout ), .Op({Op[1], and_1_out[0]}), .S(S[4]),
    .Cout(\sustracción_5_cout ));
  \Sustracción  \sustracción_6  (
    .A(A[5]), .B(B[5]), .Cin(\sustracción_5_cout ), .Op({Op[1], and_1_out[0]}), .S(S[5]),
    .Cout(\sustracción_6_cout ));
  \Sustracción  \sustracción_7  (
    .A(A[6]), .B(B[6]), .Cin(\sustracción_6_cout ), .Op({Op[1], and_1_out[0]}), .S(S[6]),
    .Cout(\sustracción_7_cout ));
  \Sustracción  \sustracción_8  (
    .A(A[7]), .B(B[7]), .Cin(\sustracción_7_cout ), .Op({Op[1], and_1_out[0]}), .S(S[7]), .Cout(out_5));
  and and_1 (and_1_out[0], not_1_out, Op[0]);
  not not_1 (not_1_out, Op[1]);
  and and_2 (and_2_out, Op[0], Op[1]);
endmodule
