// Logisim project ejemplo-logica-secuencial.circ as structural Verilog: 4 circuits, main circuit main
module main (
  input  in_1,
  input  [3:0] in_2,
  input  [1:0] in_3,
  output [3:0] _0,
  output [3:0] _1,
  output [3:0] _2,
  output [3:0] _3
);

  wire decoder_1_out0, decoder_1_out1, decoder_1_out2, decoder_1_out3;

  Decoder #(.select(2), .enable("false")) decoder_1 (
    .out0(decoder_1_out0), .out1(decoder_1_out1), .out2(decoder_1_out2), .out3(decoder_1_out3), .sel(in_3));
  registro4 registro4_1 (.in_3(in_2), .clk(in_1), .en(decoder_1_out0), .out_4(_0));
  registro4 registro4_2 (.in_3(in_2), .clk(in_1), .en(decoder_1_out1), .out_4(_1));
  registro4 registro4_3 (.in_3(in_2), .clk(in_1), .en(decoder_1_out2), .out_4(_2));
  registro4 registro4_4 (.in_3(in_2), .clk(in_1), .en(decoder_1_out3), .out_4(_3));
endmodule

module registro (
  input  clk,
  input  in,
  input  en,
  output e
);

  D_Flip_Flop d_ff_1 (.clk(clk), .D(in), .Q(e), .en(en));  // open: Qn, preset, reset
endmodule

module automata (
  input  in_1,
  output [1:0] out_2
);

  wire and_1_out, and_2_out, clock_1_out, E1_qn, E2_qn;

  and and_1 (and_1_out, E1_qn, out_2[0]);
  and and_2 (and_2_out, out_2[1], out_2[0]);
  Clock clock_1 (.out(clock_1_out));
  S_R_Flip_Flop E1 (
    .S(and_1_out), .clk(clock_1_out), .R(and_2_out), .Q(out_2[1]), .Qn(E1_qn));  // open: preset, reset, en
  S_R_Flip_Flop E2 (.S(E2_qn), .clk(clock_1_out), .R(out_2[0]), .Q(out_2[0]), .Qn(E2_qn));  // open: preset, reset, en
endmodule

module registro4 (
  input  clk,
  input  en,
  input  [3:0] in_3,
  output [3:0] out_4
);

  registro registro_1 (.clk(clk), .in(in_3[3]), .en(en), .e(out_4[3]));
  registro registro_2 (.clk(clk), .in(in_3[2]), .en(en), .e(out_4[2]));
  registro registro_3 (.clk(clk), .in(in_3[1]), .en(en), .e(out_4[1]));
  registro registro_4 (.clk(clk), .in(in_3[0]), .en(en), .e(out_4[0]));
endmodule
