// Logisim project main.circ as structural Verilog: 24 circuits, main circuit main
module main (
  input  in_1,
  output out_2
);

  // Not not_1: pin names not known; wires that end beside it: in_1, out_2
endmodule

module \and  (
  input  X,
  input  Y,
  output out_3
);

  wire transistor_1_out;

  Transistor #(.\type ("n")) transistor_1 (.in(1'b1), .out(transistor_1_out), .gate(X));
  Transistor #(.\type ("n")) transistor_2 (.in(transistor_1_out), .out(out_3), .gate(Y));
  Transistor transistor_3 (.in(1'b0), .out(out_3), .gate(Y));
  Transistor transistor_4 (.in(1'b0), .out(out_3), .gate(X));
endmodule

module \or  (
  input  X,
  input  Y,
  output out_3
);

  wire transistor_3_out;

  Transistor #(.\type ("n")) transistor_1 (.in(1'b1), .out(out_3), .gate(X));
  Transistor transistor_2 (.in(transistor_3_out), .out(out_3), .gate(X));
  Transistor transistor_3 (.in(1'b0), .out(transistor_3_out), .gate(Y));
  Transistor #(.\type ("n")) transistor_4 (.in(1'b1), .out(out_3), .gate(Y));
endmodule

module Not (
  input  X,
  output out_2
);

  Transistor transistor_1 (.in(1'b1), .out(out_2), .gate(X));
  Transistor #(.\type ("n")) transistor_2 (.in(1'b0), .out(out_2), .gate(X));
endmodule

module Nand (
  input  X,
  input  Y,
  output out_3
);

  wire transistor_3_out;

  Transistor transistor_1 (.in(1'b1), .out(out_3), .gate(X));
  Transistor #(.\type ("n")) transistor_2 (.in(transistor_3_out), .out(out_3), .gate(X));
  Transistor #(.\type ("n")) transistor_3 (.in(1'b0), .out(transistor_3_out), .gate(Y));
  Transistor transistor_4 (.in(1'b1), .out(out_3), .gate(Y));
endmodule

module Nor (
  input  X,
  input  Y,
  output out_3
);

  wire transistor_1_out;

  Transistor transistor_1 (.in(1'b1), .out(transistor_1_out), .gate(X));
  Transistor transistor_2 (.in(transistor_1_out), .out(out_3), .gate(Y));
  Transistor #(.\type ("n")) transistor_3 (.in(1'b0), .out(out_3), .gate(Y));
  Transistor #(.\type ("n")) transistor_4 (.in(1'b0), .out(out_3), .gate(X));
endmodule

module NO_A___O_B (
  input  A,
  input  B,
  output out_3
);

  wire not_1_out_2;

  Not not_1 (.X(A), .out_2(not_1_out_2));
  \or  or_1 (.X(not_1_out_2), .Y(B), .out_3(out_3));
endmodule

module A_Y___NO_B_____O_____NO_A___Y_B (
  input  A,
  input  B,
  output out_3
);

  wire and_1_out_3, and_2_out_3, not_1_out_2, not_2_out_2;

  Not not_1 (.X(A), .out_2(not_1_out_2));
  Not not_2 (.X(B), .out_2(not_2_out_2));
  \and  and_1 (.X(not_2_out_2), .Y(A), .out_3(and_1_out_3));
  \and  and_2 (.X(B), .Y(not_1_out_2), .out_3(and_2_out_3));
  \or  or_1 (.X(and_2_out_3), .Y(and_1_out_3), .out_3(out_3));
endmodule

module PRIMOS (
  input  E4,
  input  E3,
  input  E1,
  input  E0,
  output out_5
);

  wire and_1_out_5, and_2_out_5, and_3_out_5, and_4_out_5, and_5_out_5, and_6_out_5, not_1_out_2,
       not_2_out_2, not_3_out_2, not_4_out_2;

  Not not_1 (.X(E4), .out_2(not_1_out_2));
  Not not_2 (.X(E3), .out_2(not_2_out_2));
  Not not_3 (.X(E1), .out_2(not_3_out_2));
  Not not_4 (.X(E0), .out_2(not_4_out_2));
  AND and_1 (.X(E0), .Y(E1), .X_prime(not_2_out_2), .Y_prime(not_1_out_2), .out_5(and_1_out_5));
  AND and_2 (.X(not_4_out_2), .Y(E1), .X_prime(not_2_out_2), .Y_prime(not_1_out_2), .out_5(and_2_out_5));
  AND and_3 (.X(E0), .Y(not_3_out_2), .X_prime(E3), .Y_prime(not_1_out_2), .out_5(and_3_out_5));
  _6OR u_6or_1 (
    .X(and_5_out_5), .Y(and_6_out_5), .X_prime(and_4_out_5), .Y_prime(and_3_out_5),
    .X_prime_prime(and_1_out_5), .Y_prime_prime(and_2_out_5), .out_7(out_5));
  AND and_4 (.X(E0), .Y(E1), .X_prime(E3), .Y_prime(not_1_out_2), .out_5(and_4_out_5));
  AND and_5 (.X(E0), .Y(not_3_out_2), .X_prime(E3), .Y_prime(E4), .out_5(and_5_out_5));
  AND and_6 (.X(E0), .Y(E1), .X_prime(not_2_out_2), .Y_prime(E4), .out_5(and_6_out_5));
endmodule

module OR (
  input  X,
  input  Y,
  input  X_prime,
  input  Y_prime,
  output out_5
);

  wire transistor_3_out, transistor_4_out, transistor_5_out;

  Transistor #(.\type ("n")) transistor_1 (.in(1'b1), .out(out_5), .gate(X));
  Transistor transistor_2 (.in(transistor_3_out), .out(out_5), .gate(X));
  Transistor transistor_3 (.in(transistor_4_out), .out(transistor_3_out), .gate(Y));
  Transistor transistor_4 (.in(transistor_5_out), .out(transistor_4_out), .gate(X_prime));
  Transistor transistor_5 (.in(1'b0), .out(transistor_5_out), .gate(Y_prime));
  Transistor #(.\type ("n")) transistor_6 (.in(1'b1), .out(out_5), .gate(Y));
  Transistor #(.\type ("n")) transistor_7 (.in(1'b1), .out(out_5), .gate(X_prime));
  Transistor #(.\type ("n")) transistor_8 (.in(1'b1), .out(out_5), .gate(Y_prime));
endmodule

module AND (
  input  X,
  input  Y,
  input  X_prime,
  input  Y_prime,
  output out_5
);

  wire transistor_1_out, transistor_2_out, transistor_3_out;

  Transistor #(.\type ("n")) transistor_1 (.in(1'b1), .out(transistor_1_out), .gate(X));
  Transistor #(.\type ("n")) transistor_2 (.in(transistor_1_out), .out(transistor_2_out), .gate(Y));
  Transistor #(.\type ("n")) transistor_3 (.in(transistor_2_out), .out(transistor_3_out), .gate(X_prime));
  Transistor #(.\type ("n")) transistor_4 (.in(transistor_3_out), .out(out_5), .gate(Y_prime));
  Transistor transistor_5 (.in(1'b0), .out(out_5), .gate(Y));
  Transistor transistor_6 (.in(1'b0), .out(out_5), .gate(X_prime));
  Transistor transistor_7 (.in(1'b0), .out(out_5), .gate(Y_prime));
  Transistor transistor_8 (.in(1'b0), .out(out_5), .gate(X));
endmodule

module _6OR (
  input  X,
  input  Y,
  input  X_prime,
  input  Y_prime,
  input  X_prime_prime,
  input  Y_prime_prime,
  output out_7
);

  wire transistor_3_out, transistor_4_out, transistor_5_out, transistor_6_out, transistor_7_out;

  Transistor #(.\type ("n")) transistor_1 (.in(1'b1), .out(out_7), .gate(X));
  Transistor transistor_2 (.in(transistor_3_out), .out(out_7), .gate(X));
  Transistor transistor_3 (.in(transistor_4_out), .out(transistor_3_out), .gate(Y));
  Transistor transistor_4 (.in(transistor_5_out), .out(transistor_4_out), .gate(X_prime));
  Transistor transistor_5 (.in(transistor_6_out), .out(transistor_5_out), .gate(Y_prime));
  Transistor transistor_6 (.in(transistor_7_out), .out(transistor_6_out), .gate(X_prime_prime));
  Transistor transistor_7 (.in(1'b0), .out(transistor_7_out), .gate(Y_prime_prime));
  Transistor #(.\type ("n")) transistor_8 (.in(1'b1), .out(out_7), .gate(Y));
  Transistor #(.\type ("n")) transistor_9 (.in(1'b1), .out(out_7), .gate(X_prime));
  Transistor #(.\type ("n")) transistor_10 (.in(1'b1), .out(out_7), .gate(Y_prime));
  Transistor #(.\type ("n")) transistor_11 (.in(1'b1), .out(out_7), .gate(X_prime_prime));
  Transistor #(.\type ("n")) transistor_12 (.in(1'b1), .out(out_7), .gate(Y_prime_prime));
endmodule

module COMPLEMENTO_A_2 (
  input  E2,
  input  E1,
  input  E0,
  output S2,
  output S1,
  output S0
);

  wire nor_1_out_3, not_1_out_2, not_2_out_2, not_3_out_2, not_4_out_2;

  Not not_1 (.X(E2), .out_2(not_1_out_2));
  Not not_2 (.X(E1), .out_2(not_2_out_2));
  Not not_3 (.X(E0), .out_2(not_3_out_2));
  Nor nor_1 (.X(S1), .Y(S0), .out_3(nor_1_out_3));
  Xor xor_1 (.X(nor_1_out_3), .Y(not_1_out_2), .out_3(S2));
  Not not_4 (.X(S0), .out_2(not_4_out_2));
  Xor xor_2 (.X(not_4_out_2), .Y(not_2_out_2), .out_3(S1));
  Xor xor_3 (.X(1'b1), .Y(not_3_out_2), .out_3(S0));
endmodule

module Pruebas (
  input  in_1,
  input  in_2,
  output out_3
);

  wire transistor_1_out;

  Transistor transistor_1 (.in(1'b1), .out(transistor_1_out), .gate(in_2));
  Transistor #(.\type ("n")) transistor_2 (.in(transistor_1_out), .out(out_3), .gate(in_1));
  Transistor transistor_3 (.in(in_2), .out(out_3), .gate(in_1));
  Transistor #(.\type ("n")) transistor_4 (.in(1'b0), .out(transistor_1_out), .gate(in_2));
endmodule

module PLANTA_DE_SEGURIDAD (
  input  Filtro_1,
  input  Filtro_2,
  input  Filtro_3,
  output out_4,
  output out_5
);

  wire and_1_out_3, and_2_out_3, and_3_out_3, xor_1_out_3;

  Xor xor_1 (.X(Filtro_2), .Y(Filtro_3), .out_3(xor_1_out_3));
  \and  and_1 (.X(Filtro_2), .Y(Filtro_3), .out_3(and_1_out_3));
  Xor xor_2 (.X(Filtro_1), .Y(xor_1_out_3), .out_3(out_5));
  \and  and_2 (.X(Filtro_1), .Y(Filtro_2), .out_3(and_2_out_3));
  \and  and_3 (.X(Filtro_1), .Y(Filtro_3), .out_3(and_3_out_3));
  OR or_1 (.X(and_2_out_3), .Y(and_3_out_3), .X_prime(and_1_out_3), .Y_prime(and_1_out_3), .out_5(out_4));
endmodule

// Xor
module Xor (
  input  X,
  input  Y,
  output out_3
);

  wire transistor_1_out, transistor_4_out, transistor_5_out, transistor_8_out;

  Transistor transistor_1 (.in(1'b1), .out(transistor_1_out), .gate(Y));
  Transistor #(.\type ("n")) transistor_2 (.in(transistor_1_out), .out(out_3), .gate(X));
  Transistor #(.\type ("n")) transistor_3 (.in(transistor_4_out), .out(out_3), .gate(Y));
  Transistor #(.\type ("n")) transistor_4 (.in(1'b0), .out(transistor_4_out), .gate(X));
  Transistor transistor_5 (.in(1'b1), .out(transistor_5_out), .gate(X));
  Transistor #(.\type ("n")) transistor_6 (.in(transistor_5_out), .out(out_3), .gate(Y));
  Transistor transistor_7 (.in(transistor_8_out), .out(out_3), .gate(X));
  Transistor transistor_8 (.in(1'b0), .out(transistor_8_out), .gate(Y));
endmodule

module P____Q (
  input  P,
  input  Q,
  output out_3
);

  wire not_1_out_2;

  Not not_1 (.X(P), .out_2(not_1_out_2));
  \or  or_1 (.X(not_1_out_2), .Y(Q), .out_3(out_3));
endmodule

module SEGURIDAD (
  input  Filtro_1,
  input  Filtro_2,
  input  Filtro_3,
  output Notificacion,
  output Retirarse_calmadamente,
  output Evacuar_Inmediatamente
);

  wire and_1_out_3, and_2_out_3, and_3_out_3, and_4_out_3, and_5_out_3, and_6_out_3, and_7_out_3,
       and_8_out_3, or_1_out_3, or_2_out_3, or_3_out_3, xor_1_out_3, xor_2_out_3, xor_3_out_3, xor_4_out_3;

  \and  and_1 (.X(Filtro_1), .Y(Filtro_2), .out_3(and_1_out_3));
  \and  and_2 (.X(and_1_out_3), .Y(and_3_out_3), .out_3(and_2_out_3));
  \and  and_3 (.X(Filtro_1), .Y(Filtro_3), .out_3(and_3_out_3));
  \and  and_4 (.X(and_3_out_3), .Y(and_5_out_3), .out_3(and_4_out_3));
  \and  and_5 (.X(Filtro_2), .Y(Filtro_3), .out_3(and_5_out_3));
  \and  and_6 (.X(Filtro_1), .Y(Filtro_2), .out_3(and_6_out_3));
  Xor xor_1 (.X(and_6_out_3), .Y(and_7_out_3), .out_3(xor_1_out_3));
  \and  and_7 (.X(Filtro_1), .Y(Filtro_3), .out_3(and_7_out_3));
  Xor xor_2 (.X(and_7_out_3), .Y(and_8_out_3), .out_3(xor_2_out_3));
  \and  and_8 (.X(Filtro_2), .Y(Filtro_3), .out_3(and_8_out_3));
  \and  and_9 (.X(and_2_out_3), .Y(and_4_out_3), .out_3(Evacuar_Inmediatamente));
  \or  or_1 (.X(Filtro_1), .Y(Filtro_2), .out_3(or_1_out_3));
  Xor xor_3 (.X(or_1_out_3), .Y(or_2_out_3), .out_3(xor_3_out_3));
  \or  or_2 (.X(Filtro_1), .Y(Filtro_3), .out_3(or_2_out_3));
  Xor xor_4 (.X(or_2_out_3), .Y(or_3_out_3), .out_3(xor_4_out_3));
  \or  or_3 (.X(Filtro_2), .Y(Filtro_3), .out_3(or_3_out_3));
  \or  or_4 (.X(xor_1_out_3), .Y(xor_2_out_3), .out_3(Retirarse_calmadamente));
  \or  or_5 (.X(xor_3_out_3), .Y(xor_4_out_3), .out_3(Notificacion));
endmodule

module XNor (
  input  X,
  input  Y,
  output out_3
);

  wire transistor_1_out, transistor_4_out, transistor_5_out, transistor_8_out;

  Transistor transistor_1 (.in(1'b1), .out(transistor_1_out), .gate(Y));
  Transistor #(.\type ("n")) transistor_2 (.in(transistor_1_out), .out(out_3), .gate(X));
  Transistor #(.\type ("n")) transistor_3 (.in(transistor_4_out), .out(out_3), .gate(Y));
  Transistor #(.\type ("n")) transistor_4 (.in(1'b0), .out(transistor_4_out), .gate(X));
  Transistor transistor_5 (.in(1'b1), .out(transistor_5_out), .gate(X));
  Transistor #(.\type ("n")) transistor_6 (.in(transistor_5_out), .out(out_3), .gate(Y));
  Transistor transistor_7 (.in(transistor_8_out), .out(out_3), .gate(X));
  Transistor transistor_8 (.in(1'b0), .out(transistor_8_out), .gate(Y));
endmodule

module XOR (
  input  in_1,
  input  in_2,
  output out_3
);

  wire transistor_1_out;

  Transistor transistor_1 (.in(1'b1), .out(transistor_1_out), .gate(in_2));
  Transistor #(.\type ("n")) transistor_2 (.in(transistor_1_out), .out(out_3), .gate(in_1));
  Transistor transistor_3 (.in(in_2), .out(out_3), .gate(in_1));
  Transistor #(.\type ("n")) transistor_4 (.in(1'b0), .out(transistor_1_out), .gate(in_2));
endmodule

module XNOR (
  input  in_1,
  input  in_2,
  output out_3
);

  wire transistor_1_out;

  Transistor transistor_1 (.in(1'b1), .out(transistor_1_out), .gate(in_2));
  Transistor transistor_2 (.in(transistor_1_out), .out(out_3), .gate(in_1));
  Transistor #(.\type ("n")) transistor_3 (.in(in_2), .out(out_3), .gate(in_1));
  Transistor #(.\type ("n")) transistor_4 (.in(1'b0), .out(transistor_1_out), .gate(in_2));
endmodule

module Automata (
  input  in_1,
  output [1:0] out_2,
  output E1,
  output no_e1,
  output e2,
  output no_2e
);

  wire and_1_out_3, and_2_out_3, and_3_out_3, and_4_out_3, clock_1_out, not_1_out_2, or_1_out_3, or_2_out_3;

  Not not_1 (.X(in_1), .out_2(not_1_out_2));
  \and  and_1 (.X(no_2e), .Y(in_1), .out_3(and_1_out_3));
  \and  and_2 (.X(E1), .Y(in_1), .out_3(and_2_out_3));
  \and  and_3 (.X(e2), .Y(not_1_out_2), .out_3(and_3_out_3));
  Clock clock_1 (.out(clock_1_out));
  \and  and_4 (.X(no_e1), .Y(not_1_out_2), .out_3(and_4_out_3));
  \or  or_1 (.X(and_4_out_3), .Y(and_2_out_3), .out_3(or_1_out_3));
  \or  or_2 (.X(and_3_out_3), .Y(and_1_out_3), .out_3(or_2_out_3));
  D_Flip_Flop d_ff_1 (.clk(clock_1_out), .D(or_1_out_3), .Q(E1), .Qn(no_e1));  // open: preset, en, reset
  D_Flip_Flop d_ff_2 (.clk(clock_1_out), .D(or_2_out_3), .Q(e2), .Qn(no_2e));  // open: preset, en, reset

  assign out_2 = {E1, e2};
endmodule

module AND3 (
  input  X,
  input  Y,
  input  X_prime,
  output out_4
);

  wire transistor_1_out, transistor_2_out;

  Transistor #(.\type ("n")) transistor_1 (.in(1'b1), .out(transistor_1_out), .gate(X));
  Transistor #(.\type ("n")) transistor_2 (.in(transistor_1_out), .out(transistor_2_out), .gate(Y));
  Transistor #(.\type ("n")) transistor_3 (.in(transistor_2_out), .out(out_4), .gate(X_prime));
  Transistor transistor_4 (.in(1'b0), .out(out_4), .gate(X_prime));
  Transistor transistor_5 (.in(1'b0), .out(out_4), .gate(X));
  Transistor transistor_6 (.in(1'b0), .out(out_4), .gate(Y));
endmodule

module OR3 (
  input  X,
  input  Y,
  input  X_prime,
  output out_4
);

  wire transistor_5_out, transistor_6_out;

  Transistor #(.\type ("n")) transistor_1 (.in(1'b1), .out(out_4), .gate(X));
  Transistor #(.\type ("n")) transistor_2 (.in(1'b1), .out(out_4), .gate(Y));
  Transistor #(.\type ("n")) transistor_3 (.in(1'b1), .out(out_4), .gate(X_prime));
  Transistor transistor_4 (.in(transistor_5_out), .out(out_4), .gate(X));
  Transistor transistor_5 (.in(transistor_6_out), .out(transistor_5_out), .gate(Y));
  Transistor transistor_6 (.in(1'b0), .out(transistor_6_out), .gate(X_prime));
endmodule
